# Fritzing sketch audio_proj (saved by Fritzing 1.0.5)
breadboards: 1

parts:
  Part3 = Arduino Nano (Rev3.0) (ICSP)
  DFRobot_DFPlayer_Mini1 = DFRobot DFPlayer Mini [part_number=DFR0299]
  R1 = Resistor [tolerance=±5% resistance=220 package="2010 [SMD]"]
  U1 = 3.5mm Audio Jack [package=audio-jack-3.5mm-smd]
  S2 = Round Pushbutton
  R2 = Resistor [tolerance=±5% resistance=220 package="2010 [SMD]"]
  U2 = 3.5mm Audio Jack [package=audio-jack-3.5mm-smd]
  U3 = 3.5mm Audio Jack [package=audio-jack-3.5mm-smd]

nets:
  N1: Part3.GND, DFRobot_DFPlayer_Mini1.GND-1, DFRobot_DFPlayer_Mini1.GND-2, R2.Pin_1
  N2: Part3.D4, U2.RIGHT
  N3: Part3.D10, DFRobot_DFPlayer_Mini1.TX
  N4: Part3.D11/MOSI, R1.Pin_1, R2.Pin_0
  5V: Part3.5V, DFRobot_DFPlayer_Mini1.VCC
  N5: DFRobot_DFPlayer_Mini1.RX, R1.Pin_0
  N6: DFRobot_DFPlayer_Mini1.DAC_R, U1.RIGHT
  N7: DFRobot_DFPlayer_Mini1.DAC_L, U1.LEFT
  N8: S2.leg1, U3.RIGHT

notes:
  Voltage Divider
  Resistor/Yellow - 1K
  Resistor/Grey - 2K
  Female Jack prongs to DFPlayer wiring pinout
  1 - GND
  2 - Right
  3 - Left
  4 - Empty
  Female Jack Plug for button trigger
  D4 => Prong 2
  GND => Prong 1
  Button wire to Female Jack Plug prongs
  Red => Prong 2
  Black => GND
  Uses male to male amp connectors
  Uses male to male connectors to speaker
  Arduino Nano powered by USB-C connection

custom parts:
  Round Pushbutton: A generic pushbutton.
